# Fritzing sketch calorimetro_esquematico (saved by Fritzing 0.9.3b)

parts:
  Componente1 = Arduino Mega 2560 (Rev3)
  J1 = Screw terminal - 2 pins [package=THT]
  J2 = Screw terminal - 2 pins [package=THT]
  L1 = Inductor [package="400 mil [THT]"]
  Modulo_termopar_circuitar = Rotary Encoder [package=THT]
  Mosfet = A4950 [package=soicn]
  R2 = Resistor [tolerance=±20% resistance=220 package="2010 [SMD]"]
  R3 = Resistor [tolerance=±5% resistance=220 package="2010 [SMD]"]
  C1 = Capacitor [package=cap-pth-small2]  # not connected
  INA = AD9835 [package=tssop16]
  IC1 = IC, DIP package, 16 pins [chip_label=IC]  # not connected

nets (from the breadboard view):
  N1: Componente1.D21/SCL, R3.Pin_0
  N2: Componente1.D20/SDA, R2.Pin_0, INA.MCLK
  N3: Componente1.5V, R3.Pin_1, INA.SDATA
  N4: Componente1.D25, Mosfet.ent2
  N5: Componente1.D45, Modulo_termopar_circuitar.pin_3
  N6: Componente1.D51, Modulo_termopar_circuitar.pin2
  N7: Componente1.D52, Modulo_termopar_circuitar.SCK
  N8: Componente1.D53, Modulo_termopar_circuitar.pin1
  N9: Componente1.GND, Modulo_termopar_circuitar.pin_4, INA.REFOUT
  N10: J1.pin1, Mosfet.out
  N11: J1.pin2, INA.FS_ADJ
  N12: J2.pin1, L1.pin_1, Mosfet.in
  N13: J2.pin2, L1.pin_0, INA.PSEL0

custom parts:
  Rotary Encoder: Rotary Encoder from ALPS STEC12E07.
  A4950: Full-Bridge DMOS PWM Motor Driver
  AD9835: 50MHz DDS waveform generator
